// Logisim project control_logic.circ as structural Verilog: 1 circuit, main circuit control_logic
module control_logic (
  input  [31:0] inst,
  input  BrEq,
  input  BrLt,
  output PCSel,
  output RegWEn,
  output [2:0] ImmSel,
  output BrUn,
  output ASel,
  output BSel,
  output [3:0] ALUSel,
  output MemRW,
  output [1:0] WBSel,
  output CSRSel,
  output CSRWen
);

  wire and_1_out, and_3_out, and_9_out, and_10_out, and_24_out, and_25_out, and_26_out, and_27_out,
       and_28_out, Branch_comp, comparator_11_eq, comparator_12_eq, comparator_13_eq, comparator_14_eq,
       comparator_15_eq, comparator_16_eq, comparator_17_eq, comparator_18_eq, comparator_19_eq,
       comparator_20_eq, comparator_21_eq, comparator_22_eq, comparator_23_eq, comparator_24_eq,
       comparator_25_eq, comparator_26_eq, comparator_28_eq, comparator_29_eq, comparator_30_eq,
       comparator_31_eq, comparator_32_eq, comparator_33_eq, IsAND, IsANDI, IsAUIPC, IsIAType, IsILType, IsJ,
       IsJAL, IsJALR, IsLUI, IsMUL, IsMULH, IsMULHU, IsOR, IsORI, IsRType, IsSBType, IsSLL, IsSLLI, IsSLT,
       IsSLTI, IsSRA, IsSRAI, IsSRL, IsSRLI, IsSUB, IsXOR, IsXORI, not_2_out, not_3_out, or_8_out, or_13_out,
       or_14_out, or_15_out;

  Comparator #(.width(7)) comparator_1 (.a(inst[6:0]), .b(7'b0110011), .eq(IsRType));  // open: gt, lt
  Comparator #(.width(7)) comparator_2 (.a(inst[6:0]), .b(7'b0000011), .eq(IsILType));  // open: gt, lt
  Comparator #(.width(7)) comparator_3 (.a(inst[6:0]), .b(7'b0010011), .eq(IsIAType));  // open: gt, lt
  Comparator #(.width(7)) comparator_4 (.a(inst[6:0]), .b(7'b0100011), .eq(MemRW));  // open: gt, lt
  Comparator #(.width(7)) comparator_5 (.a(inst[6:0]), .b(7'b1100011), .eq(IsSBType));  // open: gt, lt
  Comparator #(.width(7)) comparator_6 (.a(inst[6:0]), .b(7'b0010111), .eq(IsAUIPC));  // open: gt, lt
  Comparator #(.width(7)) comparator_7 (.a(inst[6:0]), .b(7'b0110111), .eq(IsLUI));  // open: gt, lt
  Comparator #(.width(7)) comparator_8 (.a(inst[6:0]), .b(7'b1101111), .eq(IsJAL));  // open: gt, lt
  Comparator #(.width(7)) comparator_9 (.a(inst[6:0]), .b(7'b1100111), .eq(IsJALR));  // open: gt, lt
  Comparator #(.width(7)) comparator_10 (.a(inst[6:0]), .b(7'b1110011), .eq(CSRWen));  // open: gt, lt
  Comparator #(.width(3)) comparator_11 (.a(3'b000), .b(inst[14:12]), .eq(comparator_11_eq));  // open: gt, lt
  Comparator #(.width(7)) comparator_12 (.a(7'b0100000), .b(inst[31:25]), .eq(comparator_12_eq));  // open: gt, lt
  Comparator #(.width(7)) comparator_13 (.a(inst[31:25]), .b(7'b0000001), .eq(comparator_13_eq));  // open: gt, lt
  Comparator #(.width(3)) comparator_14 (.a(3'b001), .b(inst[14:12]), .eq(comparator_14_eq));  // open: gt, lt
  Comparator #(.width(7)) comparator_15 (.a({7{1'b0}}), .b(inst[31:25]), .eq(comparator_15_eq));  // open: gt, lt
  Comparator #(.width(7)) comparator_16 (.a(inst[31:25]), .b(7'b0000001), .eq(comparator_16_eq));  // open: gt, lt
  Comparator #(.width(3)) comparator_17 (.a(3'b010), .b(inst[14:12]), .eq(comparator_17_eq));  // open: gt, lt
  Comparator #(.width(3)) comparator_18 (.a(3'b011), .b(inst[14:12]), .eq(comparator_18_eq));  // open: gt, lt
  Comparator #(.width(3)) comparator_19 (.a(3'b100), .b(inst[14:12]), .eq(comparator_19_eq));  // open: gt, lt
  Comparator #(.width(3)) comparator_20 (.a(3'b101), .b(inst[14:12]), .eq(comparator_20_eq));  // open: gt, lt
  Comparator #(.width(7)) comparator_21 (.a({7{1'b0}}), .b(inst[31:25]), .eq(comparator_21_eq));  // open: gt, lt
  Comparator #(.width(7)) comparator_22 (.a(inst[31:25]), .b(7'b0100000), .eq(comparator_22_eq));  // open: gt, lt
  Comparator #(.width(3)) comparator_23 (.a(3'b110), .b(inst[14:12]), .eq(comparator_23_eq));  // open: gt, lt
  Comparator #(.width(3)) comparator_24 (.a(3'b111), .b(inst[14:12]), .eq(comparator_24_eq));  // open: gt, lt
  and and_1 (and_1_out, comparator_11_eq, IsRType);
  and and_2 (IsSLLI, IsIAType, comparator_14_eq);
  and and_3 (and_3_out, comparator_14_eq, IsRType);
  and and_4 (IsSLTI, IsIAType, comparator_17_eq);
  and and_5 (IsSLT, comparator_17_eq, IsRType);
  and and_6 (IsMULHU, comparator_18_eq, IsRType);
  and and_7 (IsXORI, IsIAType, comparator_19_eq);
  and and_8 (IsXOR, comparator_19_eq, IsRType);
  and and_9 (and_9_out, IsIAType, comparator_20_eq);
  and and_10 (and_10_out, comparator_20_eq, IsRType);
  and and_11 (IsORI, IsIAType, comparator_23_eq);
  and and_12 (IsOR, comparator_23_eq, IsRType);
  and and_13 (IsANDI, IsIAType, comparator_24_eq);
  and and_14 (IsAND, comparator_24_eq, IsRType);
  and and_15 (IsSUB, and_1_out, comparator_12_eq);
  and and_16 (IsMUL, and_1_out, comparator_13_eq);
  and and_17 (IsSLL, and_3_out, comparator_15_eq);
  and and_18 (IsMULH, and_3_out, comparator_16_eq);
  and and_19 (IsSRLI, and_9_out, comparator_21_eq);
  and and_20 (IsSRAI, and_9_out, comparator_22_eq);
  and and_21 (IsSRL, and_10_out, comparator_21_eq);
  and and_22 (IsSRA, and_10_out, comparator_22_eq);
  or or_1 (IsJ, IsJAL, IsJALR);
  or or_2 (ImmSel[0], MemRW, CSRWen, IsAUIPC, IsLUI);
  or or_3 (ImmSel[1], IsSBType, IsAUIPC, IsLUI);
  or or_4 (ImmSel[2], IsJAL, CSRWen);
  or or_5 (ASel, IsAUIPC, IsJAL, IsSBType);
  not not_1 (BSel, IsRType);
  nor nor_1 (RegWEn, MemRW, IsSBType);
  or or_6 (ALUSel[0], IsSLT, IsMULHU, IsXOR, IsSRA, IsAND, IsSLTI, IsXORI, IsSRAI, IsANDI);
  or or_7 (ALUSel[1], IsMUL, IsSLL, IsMULH, IsSLT, IsMULHU, IsXOR, IsOR, IsSLLI, IsSLTI, IsXORI, IsORI);
  Comparator #(.width(3)) comparator_25 (.a(3'b110), .b(inst[14:12]), .eq(comparator_25_eq));  // open: gt, lt
  Comparator #(.width(3)) comparator_26 (.a(inst[14:12]), .b(3'b111), .eq(comparator_26_eq));  // open: gt, lt
  Comparator #(.width(3)) comparator_27 (.a(inst[14:12]), .b(3'b101), .eq(CSRSel));  // open: gt, lt
  or or_8 (or_8_out, comparator_25_eq, comparator_26_eq);
  or or_9 (WBSel[0], IsILType, CSRWen);
  or or_10 (WBSel[1], CSRWen, IsJAL, IsJALR);
  or or_11 (ALUSel[2], IsSUB, IsSLL, IsMULH, IsSLT, IsSRL, IsSRA, IsSLLI, IsSLTI, IsSRLI, IsSRAI);
  or or_12 (ALUSel[3], IsSUB, IsMUL, IsMULH, IsMULHU);
  and and_23 (BrUn, IsSBType, or_8_out);
  Comparator #(.width(3)) comparator_28 (.a(3'b000), .b(inst[14:12]), .eq(comparator_28_eq));  // open: gt, lt
  Comparator #(.width(3)) comparator_29 (.a(3'b001), .b(inst[14:12]), .eq(comparator_29_eq));  // open: gt, lt
  Comparator #(.width(3)) comparator_30 (.a(inst[14:12]), .b(3'b100), .eq(comparator_30_eq));  // open: gt, lt
  Comparator #(.width(3)) comparator_31 (.a(inst[14:12]), .b(3'b110), .eq(comparator_31_eq));  // open: gt, lt
  Comparator #(.width(3)) comparator_32 (.a(inst[14:12]), .b(3'b101), .eq(comparator_32_eq));  // open: gt, lt
  Comparator #(.width(3)) comparator_33 (.a(inst[14:12]), .b(3'b111), .eq(comparator_33_eq));  // open: gt, lt
  not not_2 (not_2_out, BrEq);
  not not_3 (not_3_out, BrLt);
  and and_24 (and_24_out, IsSBType, Branch_comp);
  or or_13 (or_13_out, comparator_30_eq, comparator_31_eq);
  or or_14 (or_14_out, comparator_32_eq, comparator_33_eq);
  or or_15 (or_15_out, BrEq, not_3_out);
  or or_16 (PCSel, IsJ, and_24_out);
  and and_25 (and_25_out, BrEq, comparator_28_eq);
  and and_26 (and_26_out, not_2_out, comparator_29_eq);
  and and_27 (and_27_out, or_13_out, BrLt);
  and and_28 (and_28_out, or_14_out, or_15_out);
  or or_17 (Branch_comp, and_25_out, and_26_out, and_27_out, and_28_out);

  // Other names for the same wires on the sheet: OPCODE[6:0] = inst[6:0]; funct3[2:0] = inst[14:12];
  //   funct7[6:0] = inst[31:25]; IsCSRW = CSRWen; IsSType = MemRW

  // Notes on the sheet:
  //   INPUTS to your circuit
  //   DON'T CHANGE THE LOCATIONS OF THE INPUTS AND OUTPUTS!
  //   OUTPUT from your circuit
endmodule
