// Logisim project cpu.circ as structural Verilog: 1 circuit, main circuit cpu
module cpu (
  input  clk,
  input  [31:0] INSTRUCTION,
  input  [31:0] READ_DATA,
  output [31:0] WRITE_ADDRESS,
  output [31:0] PROGRAM_COUNTER,
  output [31:0] ra,
  output [31:0] sp,
  output [31:0] t0,
  output [31:0] t1,
  output [31:0] t2,
  output [31:0] s0,
  output [31:0] s1,
  output [31:0] a0,
  output [31:0] tohost,
  output [3:0] WRITE_ENABLE,
  output [31:0] WRITE_DATA
);

  wire ASel, BrEq, BrLt, BrUn, BSel, comparator_1_eq, comparator_2_eq, comparator_3_eq, CSRSel, CSRWen, IsSB,
       IsSH, IsSW, MemRW, PCSel, RegWEn;
  wire [1:0] WBSel;
  wire [2:0] funct3, ImmSel;
  wire [3:0] ALUSel, multiplexer_7_out, shifter_1_out, shifter_2_out;
  wire [11:0] CSR_address;
  wire [19:0] INSTRUCTION2;
  wire [31:0] ALUInputA, ALUInputB, bit_extender_1_out, CSR_din, Imm, multiplexer_1_out, multiplexer_2_out,
       PCPlus, PROGRAM_COUNTER2, ReadData1, WRITE_REGDATA;

  Adder #(.width(32)) adder_1 (.a(PROGRAM_COUNTER), .b(32'h4), .out(PCPlus));  // open: cin, cout
  Register #(.width(32)) PC (.D(multiplexer_1_out), .clk(clk), .Q(PROGRAM_COUNTER));  // open: en, clr
  Multiplexer #(.enable("false"), .width(32)) multiplexer_1 (
    .in0(PCPlus), .in1(WRITE_ADDRESS), .out(multiplexer_1_out), .sel(PCSel));
  Multiplexer #(.enable("false"), .width(32)) multiplexer_2 (
    .in0(INSTRUCTION), .in1(32'h13), .out(multiplexer_2_out), .sel(PCSel));
  Register #(.width(32)) register_1 (
    .D(multiplexer_2_out), .clk(clk), .Q({CSR_address, INSTRUCTION2[19:15], funct3, INSTRUCTION2[11:0]}));  // open: en, clr
  Register #(.width(32)) register_2 (.D(PROGRAM_COUNTER), .clk(clk), .Q(PROGRAM_COUNTER2));  // open: en, clr
  control_logic control_logic_1 (
    .CSRWen(CSRWen), .PCSel(PCSel), .RegWEn(RegWEn), .ImmSel(ImmSel), .BrUn(BrUn), .ASel(ASel), .BSel(BSel),
    .ALUSel(ALUSel), .MemRW(MemRW), .WBSel(WBSel), .CSRSel(CSRSel),
    .inst({CSR_address, INSTRUCTION2[19:15], funct3, INSTRUCTION2[11:0]}), .BrEq(BrEq), .BrLt(BrLt));
  imm_gen imm_gen_1 (.inst({CSR_address, INSTRUCTION2[19:15], funct3, INSTRUCTION2[11:0]}), .ImmSel(ImmSel), .imm(Imm));
  Multiplexer #(.enable("false"), .width(32)) multiplexer_3 (
    .in0(ReadData1), .in1(PROGRAM_COUNTER2), .out(ALUInputA), .sel(ASel));
  Multiplexer #(.enable("false"), .width(32)) multiplexer_4 (
    .in0(ReadData1), .in1(bit_extender_1_out), .out(CSR_din), .sel(CSRSel));
  assign bit_extender_1_out = {{27{1'b0}}, INSTRUCTION2[19:15]};  // Bit_Extender bit_extender_1
  Multiplexer #(.enable("false"), .select(2), .width(32)) multiplexer_5 (
    .in0(WRITE_ADDRESS), .in1(READ_DATA), .in2(PROGRAM_COUNTER), .in3(tohost), .out(WRITE_REGDATA),
    .sel(WBSel));
  regfile regfile_1 (
    .rs1(INSTRUCTION2[19:15]), .rs2(CSR_address[4:0]), .rd(INSTRUCTION2[11:7]), .Write_Data(WRITE_REGDATA),
    .RegWEn(RegWEn), .clk(clk), .ra(ra), .sp(sp), .t0(t0), .t1(t1), .t2(t2), .s0(s0), .s1(s1), .a0(a0),
    .Read_Data_1(ReadData1), .Read_Data_2(WRITE_DATA));
  branch_comp branch_comp_1 (.rs1(ReadData1), .rs2(WRITE_DATA), .BrUn(BrUn), .BrEq(BrEq), .BrLt(BrLt));
  Multiplexer #(.enable("false"), .width(32)) multiplexer_6 (.in0(WRITE_DATA), .in1(Imm), .out(ALUInputB), .sel(BSel));
  Comparator #(.width(3)) comparator_1 (.a(funct3), .b(3'b000), .eq(comparator_1_eq));  // open: gt, lt
  Comparator #(.width(3)) comparator_2 (.a(funct3), .b(3'b001), .eq(comparator_2_eq));  // open: gt, lt
  Comparator #(.width(3)) comparator_3 (.a(funct3), .b(3'b010), .eq(comparator_3_eq));  // open: gt, lt
  Multiplexer #(.enable("false"), .width(4)) multiplexer_7 (
    .in0(4'b1111), .in1(shifter_1_out), .out(multiplexer_7_out), .sel(IsSH));
  Shifter #(.shift("rl"), .width(4)) shifter_1 (.in(4'b0011), .\dist (WRITE_ADDRESS[1:0]), .out(shifter_1_out));
  alu alu_1 (.Result(WRITE_ADDRESS), .A(ALUInputA), .B(ALUInputB), .ALUSel(ALUSel));
  csr csr_1 (.CSR_address(CSR_address), .CSR_din(CSR_din), .CSR_WE(CSRWen), .clk(clk), .tohost(tohost));
  and and_1 (IsSB, MemRW, comparator_1_eq);
  and and_2 (IsSH, MemRW, comparator_2_eq);
  and and_3 (IsSW, MemRW, comparator_3_eq);
  Multiplexer #(.enable("false"), .width(4)) multiplexer_8 (
    .in0(multiplexer_7_out), .in1(shifter_2_out), .out(WRITE_ENABLE), .sel(IsSB));
  Shifter #(.shift("rl"), .width(4)) shifter_2 (.in(4'b0001), .\dist (WRITE_ADDRESS[1:0]), .out(shifter_2_out));

  // Other names for the same wires on the sheet: ALUResult[31:0] = WRITE_ADDRESS; rd[4:0] = INSTRUCTION2[11:7];
  //   INSTRUCTION2 (some bits) = {CSR_address, funct3}; rs1[4:0] = INSTRUCTION2[19:15]; rs2[4:0] = CSR_address[4:0];
  //   ReadData2[31:0] = WRITE_DATA

  // Notes on the sheet:
  //   Output to IMEM
  //   IMEM (do **NOT** move this)
  //   Inputs from IMEM
  //   It is OK to move the PC, RegFile, ALU, MEM, Branch Comp, Imm Gen, and Control Logic to wherever is most convenient for you when constructing your CPU, and to delete this text
  //   Inputs/Outputs for testing. Do **NOT** move these.
  //   Outputs To DMEM
  //   DMEM (do **NOT** move this)
  //   Inputs From DMEM
endmodule
