// Logisim project imm_gen.circ as structural Verilog: 1 circuit, main circuit imm_gen
module imm_gen (
  input  [31:0] inst,
  input  [2:0] ImmSel,
  output [31:0] imm
);

  wire [31:0] bit_extender_1_out, bit_extender_2_out, bit_extender_3_out, bit_extender_4_out,
       bit_extender_5_out, shifter_1_out;

  assign bit_extender_1_out = {{12{inst[31]}}, inst[31:12]};  // Bit_Extender bit_extender_1
  assign bit_extender_2_out = {{20{inst[31]}}, inst[31:20]};  // Bit_Extender bit_extender_2
  assign bit_extender_3_out = {{20{inst[31]}}, {inst[31:25], inst[11:7]}};  // Bit_Extender bit_extender_3
  assign bit_extender_4_out = {{20{inst[31]}}, {inst[31:25], inst[11:8], 1'b0}};  // Bit_Extender bit_extender_4
  Shifter #(.width(32)) shifter_1 (.in(bit_extender_1_out), .\dist (5'b01100), .out(shifter_1_out));
  assign bit_extender_5_out = {{11{inst[31]}}, {inst[31], inst[19:12], inst[20], inst[30:21], 1'b0}};  // Bit_Extender bit_extender_5
  Multiplexer #(.enable("false"), .select(3), .width(32)) multiplexer_1 (
    .in0(bit_extender_2_out), .in1(bit_extender_3_out), .in2(bit_extender_4_out), .in3(shifter_1_out),
    .in4(bit_extender_5_out), .out(imm), .sel(ImmSel));  // open: in5, in6, in7

  // Other names for the same wires on the sheet: ImmB[11:1] = {inst[31:25], inst[11:8]};
  //   ImmS[11:0] = {inst[31:25], inst[11:7]}; Ins8_11[3:0] = inst[11:8]; ImmI[11:0] = inst[31:20];
  //   ImmJ[20:1] = {inst[31], inst[19:12], inst[20], inst[30:21]}; ImmU[19:0] = inst[31:12];
  //   Ins21_24[3:0] = inst[24:21]; Ins25_30[5:0] = inst[30:25]; Ins20 = inst[20]; Ins12_19[7:0] = inst[19:12];
  //   Ins31 = inst[31]; Ins7 = inst[7]

  // Notes on the sheet:
  //   INPUTS to your circuit
  //   DON'T CHANGE THE LOCATIONS OF THE INPUTS AND OUTPUTS!
  //   OUTPUT from your circuit
endmodule
